// Logisim project TP1_v3.circ as structural Verilog: 13 circuits, main circuit main
module main (
);

  wire bcd_7s_1_a, bcd_7s_1_b, bcd_7s_1_c, bcd_7s_1_d, bcd_7s_1_e, bcd_7s_1_f, bcd_7s_1_g, bcd_7s_2_a,
       bcd_7s_2_b, bcd_7s_2_c, bcd_7s_2_d, bcd_7s_2_e, bcd_7s_2_f, bcd_7s_2_g, bcd_7s_3_a, bcd_7s_3_b,
       bcd_7s_3_c, bcd_7s_3_d, bcd_7s_3_e, bcd_7s_3_f, bcd_7s_3_g, bcd_7s_4_a, bcd_7s_4_b, bcd_7s_4_c,
       bcd_7s_4_d, bcd_7s_4_e, bcd_7s_4_f, bcd_7s_4_g, bcd_7s_5_a, bcd_7s_5_b, bcd_7s_5_c, bcd_7s_5_d,
       bcd_7s_5_e, bcd_7s_5_f, bcd_7s_5_g, bcd_7s_6_a, bcd_7s_6_b, bcd_7s_6_c, bcd_7s_6_d, bcd_7s_6_e,
       bcd_7s_6_f, bcd_7s_6_g, bcd_7s_7_a, bcd_7s_7_b, bcd_7s_7_c, bcd_7s_7_d, bcd_7s_7_e, bcd_7s_7_f,
       bcd_7s_7_g, bcd_7s_8_a, bcd_7s_8_b, bcd_7s_8_c, bcd_7s_8_d, bcd_7s_8_e, bcd_7s_8_f, bcd_7s_8_g,
       bcd_7s_9_a, bcd_7s_9_b, bcd_7s_9_c, bcd_7s_9_d, bcd_7s_9_e, bcd_7s_9_f, bcd_7s_9_g, bcd_7s_10_a,
       bcd_7s_10_b, bcd_7s_10_c, bcd_7s_10_d, bcd_7s_10_e, bcd_7s_10_f, bcd_7s_10_g, bcd_7s_11_a,
       bcd_7s_11_b, bcd_7s_11_c, bcd_7s_11_d, bcd_7s_11_e, bcd_7s_11_f, bcd_7s_11_g, bcd_7s_12_a,
       bcd_7s_12_b, bcd_7s_12_c, bcd_7s_12_d, bcd_7s_12_e, bcd_7s_12_f, bcd_7s_12_g, bcd_7s_13_a,
       bcd_7s_13_b, bcd_7s_13_c, bcd_7s_13_d, bcd_7s_13_e, bcd_7s_13_f, bcd_7s_13_g, clock_1_out,
       Horloge_1_clk_out, Microprocesseur_1_ld_to_cache, Microprocesseur_1_sd_to_cache;
  wire [3:0] Periph_listener_1_address_000_value_3to0, Periph_listener_1_address_000_value_7to4,
       Periph_listener_1_address_000_value_bto8, Periph_listener_1_address_001_value_3to0,
       Periph_listener_1_address_001_value_7to4, Periph_listener_1_address_001_value_bto8,
       Periph_listener_1_address_002_value_3to0, Periph_listener_1_address_002_value_7to4,
       Periph_listener_1_address_002_value_bto8;
  wire [11:0] Memoire_des_donnees_dout, Memoire_instructions_dout, Microprocesseur_1_address_to_cache,
       Microprocesseur_1_address_to_mem_instr, Microprocesseur_1_sd_data_to_cache;

  Clock clock_1 (.out(clock_1_out));
  _7_Segment_Display u_7_segment_display_1 (
    .g(bcd_7s_1_g), .f(bcd_7s_1_f), .a(bcd_7s_1_a), .b(bcd_7s_1_b), .e(bcd_7s_1_e), .d(bcd_7s_1_d),
    .c(bcd_7s_1_c));  // open: dp
  BCD_7S bcd_7s_1 (
    .C(bcd_7s_1_c), .E(bcd_7s_1_e), .G(bcd_7s_1_g), .A(bcd_7s_1_a), .D(bcd_7s_1_d), .F(bcd_7s_1_f),
    .B(bcd_7s_1_b));  // open: Data
  // Binary_to_BCD_converter #(.binvalue(12)) binary_to_bcd_converter_1: pin names not known
  _7_Segment_Display u_7_segment_display_2 (
    .g(bcd_7s_2_g), .f(bcd_7s_2_f), .a(bcd_7s_2_a), .b(bcd_7s_2_b), .e(bcd_7s_2_e), .d(bcd_7s_2_d),
    .c(bcd_7s_2_c));  // open: dp
  BCD_7S bcd_7s_2 (
    .C(bcd_7s_2_c), .E(bcd_7s_2_e), .G(bcd_7s_2_g), .A(bcd_7s_2_a), .D(bcd_7s_2_d), .F(bcd_7s_2_f),
    .B(bcd_7s_2_b));  // open: Data
  Microprocesseur Microprocesseur_1 (
    .ld_data_from_cache(Memoire_des_donnees_dout), .data_from_mem_instr(Memoire_instructions_dout),
    .Clk(Horloge_1_clk_out), .ready_from_cache(1'b1), .sd_to_cache(Microprocesseur_1_sd_to_cache),
    .address_to_cache(Microprocesseur_1_address_to_cache),
    .address_to_mem_instr(Microprocesseur_1_address_to_mem_instr),
    .sd_data_to_cache(Microprocesseur_1_sd_data_to_cache), .ld_to_cache(Microprocesseur_1_ld_to_cache));
  _7_Segment_Display u_7_segment_display_3 (
    .g(bcd_7s_3_g), .f(bcd_7s_3_f), .a(bcd_7s_3_a), .b(bcd_7s_3_b), .e(bcd_7s_3_e), .d(bcd_7s_3_d),
    .c(bcd_7s_3_c));  // open: dp
  _7_Segment_Display u_7_segment_display_4 (
    .g(bcd_7s_4_g), .f(bcd_7s_4_f), .a(bcd_7s_4_a), .b(bcd_7s_4_b), .e(bcd_7s_4_e), .d(bcd_7s_4_d),
    .c(bcd_7s_4_c));  // open: dp
  BCD_7S bcd_7s_3 (
    .C(bcd_7s_3_c), .E(bcd_7s_3_e), .G(bcd_7s_3_g), .A(bcd_7s_3_a), .D(bcd_7s_3_d), .F(bcd_7s_3_f),
    .B(bcd_7s_3_b));  // open: Data
  BCD_7S bcd_7s_4 (
    .C(bcd_7s_4_c), .E(bcd_7s_4_e), .G(bcd_7s_4_g), .A(bcd_7s_4_a), .D(bcd_7s_4_d), .F(bcd_7s_4_f),
    .B(bcd_7s_4_b));  // open: Data
  Horloge Horloge_1 (
    .Clk_in(clock_1_out), .Data(Microprocesseur_1_sd_data_to_cache),
    .Listen_address(Microprocesseur_1_address_to_cache), .En(Microprocesseur_1_sd_to_cache),
    .Clk_out(Horloge_1_clk_out));  // open: Count
  _7_Segment_Display u_7_segment_display_5 (
    .g(bcd_7s_5_g), .f(bcd_7s_5_f), .a(bcd_7s_5_a), .b(bcd_7s_5_b), .e(bcd_7s_5_e), .d(bcd_7s_5_d),
    .c(bcd_7s_5_c));  // open: dp
  _7_Segment_Display u_7_segment_display_6 (
    .g(bcd_7s_6_g), .f(bcd_7s_6_f), .a(bcd_7s_6_a), .b(bcd_7s_6_b), .e(bcd_7s_6_e), .d(bcd_7s_6_d),
    .c(bcd_7s_6_c));  // open: dp
  BCD_7S bcd_7s_5 (
    .Data(Periph_listener_1_address_002_value_bto8), .C(bcd_7s_5_c), .E(bcd_7s_5_e), .G(bcd_7s_5_g),
    .A(bcd_7s_5_a), .D(bcd_7s_5_d), .F(bcd_7s_5_f), .B(bcd_7s_5_b));
  _7_Segment_Display u_7_segment_display_7 (
    .g(bcd_7s_7_g), .f(bcd_7s_7_f), .a(bcd_7s_7_a), .b(bcd_7s_7_b), .e(bcd_7s_7_e), .d(bcd_7s_7_d),
    .c(bcd_7s_7_c));  // open: dp
  BCD_7S bcd_7s_6 (
    .Data(Periph_listener_1_address_002_value_7to4), .C(bcd_7s_6_c), .E(bcd_7s_6_e), .G(bcd_7s_6_g),
    .A(bcd_7s_6_a), .D(bcd_7s_6_d), .F(bcd_7s_6_f), .B(bcd_7s_6_b));
  _7_Segment_Display u_7_segment_display_8 (
    .g(bcd_7s_8_g), .f(bcd_7s_8_f), .a(bcd_7s_8_a), .b(bcd_7s_8_b), .e(bcd_7s_8_e), .d(bcd_7s_8_d),
    .c(bcd_7s_8_c));  // open: dp
  BCD_7S bcd_7s_7 (
    .Data(Periph_listener_1_address_002_value_3to0), .C(bcd_7s_7_c), .E(bcd_7s_7_e), .G(bcd_7s_7_g),
    .A(bcd_7s_7_a), .D(bcd_7s_7_d), .F(bcd_7s_7_f), .B(bcd_7s_7_b));
  BCD_7S bcd_7s_8 (
    .Data(Periph_listener_1_address_001_value_bto8), .C(bcd_7s_8_c), .E(bcd_7s_8_e), .G(bcd_7s_8_g),
    .A(bcd_7s_8_a), .D(bcd_7s_8_d), .F(bcd_7s_8_f), .B(bcd_7s_8_b));
  _7_Segment_Display u_7_segment_display_9 (
    .g(bcd_7s_9_g), .f(bcd_7s_9_f), .a(bcd_7s_9_a), .b(bcd_7s_9_b), .e(bcd_7s_9_e), .d(bcd_7s_9_d),
    .c(bcd_7s_9_c));  // open: dp
  _7_Segment_Display u_7_segment_display_10 (
    .g(bcd_7s_10_g), .f(bcd_7s_10_f), .a(bcd_7s_10_a), .b(bcd_7s_10_b), .e(bcd_7s_10_e), .d(bcd_7s_10_d),
    .c(bcd_7s_10_c));  // open: dp
  BCD_7S bcd_7s_9 (
    .Data(Periph_listener_1_address_001_value_7to4), .C(bcd_7s_9_c), .E(bcd_7s_9_e), .G(bcd_7s_9_g),
    .A(bcd_7s_9_a), .D(bcd_7s_9_d), .F(bcd_7s_9_f), .B(bcd_7s_9_b));
  RAM #(.addrWidth(12), .dataWidth(12), .trigger("high"), .\type ("nonvolatile")) Memoire_instructions (
    .addr(Microprocesseur_1_address_to_mem_instr), .dout(Memoire_instructions_dout));  // open: we, oe, din
  RAM #(.addrWidth(12), .dataWidth(12), .trigger("falling"), .\type ("nonvolatile")) Memoire_des_donnees (
    .addr(Microprocesseur_1_address_to_cache), .we(Microprocesseur_1_sd_to_cache),
    .oe(Microprocesseur_1_ld_to_cache), .clk(Horloge_1_clk_out), .din(Microprocesseur_1_sd_data_to_cache),
    .dout(Memoire_des_donnees_dout));
  _7_Segment_Display u_7_segment_display_11 (
    .g(bcd_7s_11_g), .f(bcd_7s_11_f), .a(bcd_7s_11_a), .b(bcd_7s_11_b), .e(bcd_7s_11_e), .d(bcd_7s_11_d),
    .c(bcd_7s_11_c));  // open: dp
  BCD_7S bcd_7s_10 (
    .Data(Periph_listener_1_address_001_value_3to0), .C(bcd_7s_10_c), .E(bcd_7s_10_e), .G(bcd_7s_10_g),
    .A(bcd_7s_10_a), .D(bcd_7s_10_d), .F(bcd_7s_10_f), .B(bcd_7s_10_b));
  _7_Segment_Display u_7_segment_display_12 (
    .g(bcd_7s_12_g), .f(bcd_7s_12_f), .a(bcd_7s_12_a), .b(bcd_7s_12_b), .e(bcd_7s_12_e), .d(bcd_7s_12_d),
    .c(bcd_7s_12_c));  // open: dp
  BCD_7S bcd_7s_11 (
    .Data(Periph_listener_1_address_000_value_bto8), .C(bcd_7s_11_c), .E(bcd_7s_11_e), .G(bcd_7s_11_g),
    .A(bcd_7s_11_a), .D(bcd_7s_11_d), .F(bcd_7s_11_f), .B(bcd_7s_11_b));
  BCD_7S bcd_7s_12 (
    .Data(Periph_listener_1_address_000_value_7to4), .C(bcd_7s_12_c), .E(bcd_7s_12_e), .G(bcd_7s_12_g),
    .A(bcd_7s_12_a), .D(bcd_7s_12_d), .F(bcd_7s_12_f), .B(bcd_7s_12_b));
  _7_Segment_Display u_7_segment_display_13 (
    .g(bcd_7s_13_g), .f(bcd_7s_13_f), .a(bcd_7s_13_a), .b(bcd_7s_13_b), .e(bcd_7s_13_e), .d(bcd_7s_13_d),
    .c(bcd_7s_13_c));  // open: dp
  BCD_7S bcd_7s_13 (
    .Data(Periph_listener_1_address_000_value_3to0), .C(bcd_7s_13_c), .E(bcd_7s_13_e), .G(bcd_7s_13_g),
    .A(bcd_7s_13_a), .D(bcd_7s_13_d), .F(bcd_7s_13_f), .B(bcd_7s_13_b));
  Periph_listener Periph_listener_1 (
    .Clk(Horloge_1_clk_out), .Data(Microprocesseur_1_sd_data_to_cache),
    .Address(Microprocesseur_1_address_to_cache), .En(Microprocesseur_1_sd_to_cache),
    .address_000_value_3to0(Periph_listener_1_address_000_value_3to0),
    .address_000_value_7to4(Periph_listener_1_address_000_value_7to4),
    .address_000_value_Bto8(Periph_listener_1_address_000_value_bto8),
    .address_001_value_3to0(Periph_listener_1_address_001_value_3to0),
    .address_001_value_7to4(Periph_listener_1_address_001_value_7to4),
    .address_001_value_Bto8(Periph_listener_1_address_001_value_bto8),
    .address_002_value_3to0(Periph_listener_1_address_002_value_3to0),
    .address_002_value_7to4(Periph_listener_1_address_002_value_7to4),
    .address_002_value_Bto8(Periph_listener_1_address_002_value_bto8));
endmodule

module Microprocesseur (
  input  [11:0] ld_data_from_cache,
  input  [11:0] data_from_mem_instr,
  input  Clk,
  input  ready_from_cache,
  output [11:0] address_to_cache,
  output [11:0] address_to_mem_instr,
  output [11:0] sd_data_to_cache,
  output ld_to_cache,
  output sd_to_cache
);

  wire and_2_out, and_3_out, branch_unit_1_is_taken_branch, comparator_1_eq, comparator_2_eq, decoder_2_out0,
       decoder_2_out1, decoder_2_out2, decoder_2_out3, decoder_2_out4, decoder_2_out5, decoder_2_out6,
       decoder_2_out7, decoder_2_out8, decoder_2_out9, decoder_2_out12, decoder_2_out13, decoder_2_out14,
       decoder_2_out15, decoder_3_out0, decoder_3_out1, decoder_3_out2, decoder_3_out3, decoder_3_out4,
       decoder_3_out5, decoder_3_out6, decoder_3_out7, decoder_3_out8, decoder_3_out9, decoder_3_out10,
       decoder_3_out12, decoder_3_out13, IS_ALU, IS_LOAD, IS_NOP, IS_STORE, not_1_out, not_2_out, or_1_out,
       WRITE_EN;
  wire [1:0] EX_MEM_1_rd_out, ID_EX_1_rd_out, priority_encoder_1_out, RD_IN;
  wire [11:0] adder_1_out, alu_1_result, branch_unit_1_npc, DATA_IN, ID_EX_1_a_out, ID_EX_1_b_out,
       ID_EX_1_npc_out, IF_ID_1_npc_out, MEM_WB_1_load_out, MEM_WB_1_result_out, multiplexer_1_out,
       Registers_1_a, Registers_1_b, TO_SCREEN_1, TO_SCREEN_2, TO_SCREEN_3, TO_SCREEN_4;

  Register #(.trigger("falling"), .width(12)) PC (
    .D(multiplexer_1_out), .en(1'b1), .clk(Clk), .Q(address_to_mem_instr), .clr(1'b0));
  Hex_Digit_Display hex_digit_display_1 (.value(data_from_mem_instr[11:8]));  // open: dp
  Adder #(.width(12)) adder_1 (.a(12'h1), .b(address_to_mem_instr), .out(adder_1_out));  // open: cin, cout
  Hex_Digit_Display hex_digit_display_2 (.value(data_from_mem_instr[7:4]));  // open: dp
  Multiplexer #(.width(12)) multiplexer_1 (
    .in0(adder_1_out), .in1(branch_unit_1_npc), .out(multiplexer_1_out), .sel(branch_unit_1_is_taken_branch));
  Hex_Digit_Display hex_digit_display_3 (.value(data_from_mem_instr[3:0]));  // open: dp
  IF_ID IF_ID_1 (
    .En(Clk), .NPC_in(multiplexer_1_out), .IR_in(data_from_mem_instr), .Clk(Clk), .NPC_out(IF_ID_1_npc_out),
    .IR_out(TO_SCREEN_1));
  Hex_Digit_Display hex_digit_display_4 (.value(TO_SCREEN_1[11:8]));  // open: dp
  Hex_Digit_Display hex_digit_display_5 (.value(TO_SCREEN_1[7:4]));  // open: dp
  Hex_Digit_Display hex_digit_display_6 (.value(TO_SCREEN_1[3:0]));  // open: dp
  Registers Registers_1 (
    .rs1(TO_SCREEN_1[5:4]), .rs2(TO_SCREEN_1[3:2]), .rd(RD_IN), .Write_en(WRITE_EN), .Data(DATA_IN),
    .Clk(Clk), .A(Registers_1_a), .B(Registers_1_b));
  Hex_Digit_Display hex_digit_display_7 (.value(TO_SCREEN_2[11:8]));  // open: dp
  Hex_Digit_Display hex_digit_display_8 (.value(TO_SCREEN_2[7:4]));  // open: dp
  Hex_Digit_Display hex_digit_display_9 (.value(TO_SCREEN_2[3:0]));  // open: dp
  Branch_unit branch_unit_1 (
    .IR(TO_SCREEN_1), .NPC_in(IF_ID_1_npc_out), .A(Registers_1_a),
    .is_taken_branch(branch_unit_1_is_taken_branch), .NPC(branch_unit_1_npc));  // open: is_instr_branch, Result
  Hex_Digit_Display hex_digit_display_10 (.value(TO_SCREEN_3[11:8]));  // open: dp
  ID_EX ID_EX_1 (
    .A_in(Registers_1_a), .B_in(Registers_1_b), .Clk(Clk), .NPC_in(IF_ID_1_npc_out), .IR_in(TO_SCREEN_1),
    .En(Clk), .rd_in(TO_SCREEN_1[7:6]), .A_out(ID_EX_1_a_out), .B_out(ID_EX_1_b_out),
    .NPC_out(ID_EX_1_npc_out), .IR_out(TO_SCREEN_2), .rd_out(ID_EX_1_rd_out));
  Hex_Digit_Display hex_digit_display_11 (.value(TO_SCREEN_3[7:4]));  // open: dp
  Hex_Digit_Display hex_digit_display_12 (.value(TO_SCREEN_3[3:0]));  // open: dp
  ALU alu_1 (.Instruction(TO_SCREEN_2), .A(ID_EX_1_a_out), .B(ID_EX_1_b_out), .Result(alu_1_result));
  Hex_Digit_Display hex_digit_display_13 (.value(TO_SCREEN_4[11:8]));  // open: dp
  Hex_Digit_Display hex_digit_display_14 (.value(TO_SCREEN_4[7:4]));  // open: dp
  Hex_Digit_Display hex_digit_display_15 (.value(TO_SCREEN_4[3:0]));  // open: dp
  EX_MEM EX_MEM_1 (
    .Branch_Taken_in(branch_unit_1_is_taken_branch), .Result_in(alu_1_result), .B_in(ID_EX_1_b_out),
    .NPC_in(ID_EX_1_npc_out), .IR_in(TO_SCREEN_2), .rd_in(ID_EX_1_rd_out), .En(Clk), .Clk(Clk),
    .IR_out(TO_SCREEN_3), .rd_out(EX_MEM_1_rd_out), .Result_out(address_to_cache), .B_out(sd_data_to_cache));  // open: NPC_out, Branch_Taken_out
  Decoder #(.enable("false"), .select(4)) decoder_1 (
    .out10(ld_to_cache), .out11(sd_to_cache), .sel(TO_SCREEN_3[11:8]));  // open: out0, out1, out2, out3, out4, out5, out6, out7, out8, out9, out12, out13, out14, out15
  MEM_WB MEM_WB_1 (
    .rd_in(EX_MEM_1_rd_out), .Load_in(ld_data_from_cache), .Clk(Clk), .En(Clk), .IR_in(TO_SCREEN_3),
    .Result_in(address_to_cache), .IR_out(TO_SCREEN_4), .rd_out(RD_IN), .Result_out(MEM_WB_1_result_out),
    .Load_out(MEM_WB_1_load_out));
  Multiplexer #(.select(2), .width(12)) multiplexer_2 (
    .in0(MEM_WB_1_result_out), .in1(MEM_WB_1_load_out), .in2({12{1'b0}}), .in3({12{1'b0}}), .out(DATA_IN),
    .sel(priority_encoder_1_out));
  Priority_Encoder #(.select(2)) priority_encoder_1 (
    .in0(IS_ALU), .in1(IS_LOAD), .in2(IS_STORE), .in3(IS_NOP), .out(priority_encoder_1_out));
  Hex_Digit_Display hex_digit_display_16 (.value(DATA_IN[11:8]));  // open: dp
  Hex_Digit_Display hex_digit_display_17 (.value(DATA_IN[7:4]));  // open: dp
  Hex_Digit_Display hex_digit_display_18 (.value(DATA_IN[3:0]));  // open: dp
  Decoder #(.enable("false"), .select(4)) decoder_2 (
    .out0(decoder_2_out0), .out1(decoder_2_out1), .out2(decoder_2_out2), .out3(decoder_2_out3),
    .out4(decoder_2_out4), .out5(decoder_2_out5), .out6(decoder_2_out6), .out7(decoder_2_out7),
    .out8(decoder_2_out8), .out9(decoder_2_out9), .out10(IS_LOAD), .out11(IS_STORE), .out12(decoder_2_out12),
    .out13(decoder_2_out13), .out14(decoder_2_out14), .out15(decoder_2_out15), .sel(TO_SCREEN_4[11:8]));
  Comparator #(.width(2)) comparator_1 (.a(TO_SCREEN_4[1:0]), .b(2'b00), .eq(comparator_1_eq));  // open: gt, lt
  and and_1 (IS_NOP, comparator_1_eq, decoder_2_out0);
  not not_1 (not_1_out, comparator_2_eq);
  Comparator #(.width(2)) comparator_2 (.a(TO_SCREEN_4[1:0]), .b(2'b00), .eq(comparator_2_eq));  // open: gt, lt
  Decoder #(.enable("false"), .select(4)) decoder_3 (
    .out0(decoder_3_out0), .out1(decoder_3_out1), .out2(decoder_3_out2), .out3(decoder_3_out3),
    .out4(decoder_3_out4), .out5(decoder_3_out5), .out6(decoder_3_out6), .out7(decoder_3_out7),
    .out8(decoder_3_out8), .out9(decoder_3_out9), .out10(decoder_3_out10), .out12(decoder_3_out12),
    .out13(decoder_3_out13), .sel(TO_SCREEN_4[11:8]));  // open: out11, out14, out15
  not not_2 (not_2_out, IS_NOP);
  and and_2 (and_2_out, not_1_out, decoder_3_out0);
  or or_1 (or_1_out, decoder_3_out1, decoder_3_out2, decoder_3_out3, decoder_3_out4, decoder_3_out5, decoder_3_out6, decoder_3_out7, decoder_3_out8, decoder_3_out9, decoder_3_out10, decoder_3_out12, decoder_3_out13);
  and and_3 (and_3_out, not_2_out, decoder_2_out0);
  or or_2 (WRITE_EN, and_2_out, or_1_out);
  or or_3 (IS_ALU, and_3_out, decoder_2_out1, decoder_2_out2, decoder_2_out3, decoder_2_out4, decoder_2_out5, decoder_2_out6, decoder_2_out8, decoder_2_out9, decoder_2_out7, decoder_2_out15, decoder_2_out12, decoder_2_out13, decoder_2_out14);

  // Other names for the same wires on the sheet: adress_to_cache[11:0] = address_to_cache; Clock = Clk;
  //   DATA_SCREEN[11:0] = DATA_IN; TO_SCREEN_0[11:0] = data_from_mem_instr

  // Notes on the sheet:
  //   POURQUOI LA PREMIERE INSTRUCTION EST ECRASEE ?
  //   Pass rd to write back to the proper register
  //   TODO
  //   Check if instruction writes to rd
  //   Assuming the two instructions reserved for the future never happen
  //   Exlude nop
endmodule

module IF_ID (
  input  Clk,
  input  En,
  input  [11:0] NPC_in,
  input  [11:0] IR_in,
  output [11:0] NPC_out,
  output [11:0] IR_out
);

  Register #(.width(12)) NPC_reg12 (.D(NPC_in), .en(En), .clk(Clk), .Q(NPC_out));  // open: clr
  Register #(.width(12)) IR_reg12 (.D(IR_in), .en(En), .clk(Clk), .Q(IR_out));  // open: clr
endmodule

module ID_EX (
  input  Clk,
  input  En,
  input  [11:0] A_in,
  input  [11:0] B_in,
  input  [11:0] NPC_in,
  input  [11:0] IR_in,
  input  [1:0] rd_in,
  output [11:0] A_out,
  output [11:0] B_out,
  output [11:0] NPC_out,
  output [11:0] IR_out,
  output [1:0] rd_out
);

  Register #(.width(12)) A_reg12 (.D(A_in), .en(En), .clk(Clk), .Q(A_out));  // open: clr
  Register #(.width(12)) B_reg12 (.D(B_in), .en(En), .clk(Clk), .Q(B_out));  // open: clr
  Register #(.width(12)) NPC_reg12 (.D(NPC_in), .en(En), .clk(Clk), .Q(NPC_out));  // open: clr
  Register #(.width(12)) IR_reg12 (.D(IR_in), .en(En), .clk(Clk), .Q(IR_out));  // open: clr
  Register #(.width(2)) rd_reg2 (.D(rd_in), .en(En), .clk(Clk), .Q(rd_out));  // open: clr
endmodule

module EX_MEM (
  input  Clk,
  input  En,
  input  [11:0] NPC_in,
  input  [11:0] IR_in,
  input  [1:0] rd_in,
  input  Branch_Taken_in,
  input  [11:0] Result_in,
  input  [11:0] B_in,
  output [11:0] NPC_out,
  output [11:0] IR_out,
  output [1:0] rd_out,
  output Branch_Taken_out,
  output [11:0] Result_out,
  output [11:0] B_out
);

  Register #(.width(12)) NPC_reg12 (.D(NPC_in), .en(En), .clk(Clk), .Q(NPC_out));  // open: clr
  Register #(.width(12)) IR_reg12 (.D(IR_in), .en(En), .clk(Clk), .Q(IR_out));  // open: clr
  Register #(.width(2)) rd_reg2 (.D(rd_in), .en(En), .clk(Clk), .Q(rd_out));  // open: clr
  Register #(.width(1)) Branch_reg1 (.D(Branch_Taken_in), .en(En), .clk(Clk), .Q(Branch_Taken_out));  // open: clr
  Register #(.width(12)) Result_reg12 (.D(Result_in), .en(En), .clk(Clk), .Q(Result_out));  // open: clr
  Register #(.width(12)) B_reg12 (.D(B_in), .en(En), .clk(Clk), .Q(B_out));  // open: clr
endmodule

module MEM_WB (
  input  Clk,
  input  En,
  input  [11:0] IR_in,
  input  [1:0] rd_in,
  input  [11:0] Result_in,
  input  [11:0] Load_in,
  output [11:0] IR_out,
  output [1:0] rd_out,
  output [11:0] Result_out,
  output [11:0] Load_out
);

  wire and_1_out, comparator_1_eq, not_1_out;

  Register #(.width(12)) IR_reg12 (.D(IR_in), .en(En), .clk(Clk), .Q(IR_out));  // open: clr
  Register #(.width(2)) register_1 (.D(rd_in), .en(En), .clk(Clk), .Q(rd_out));  // open: clr
  Register #(.width(12)) Result_reg12 (.D(Result_in), .en(not_1_out), .clk(Clk), .Q(Result_out));  // open: clr
  Register #(.width(12)) Load_reg12 (.D(Load_in), .en(not_1_out), .clk(Clk), .Q(Load_out));  // open: clr
  Comparator #(.width(12)) comparator_1 (.a(IR_in), .b({12{1'b0}}), .eq(comparator_1_eq));  // open: gt, lt
  and and_1 (and_1_out, comparator_1_eq, En);
  not not_1 (not_1_out, and_1_out);
endmodule

module ALU (
  input  [11:0] Instruction,
  input  [11:0] A,
  input  [11:0] B,
  output [11:0] Result
);

  wire [1:0] decode_1_pin_1to0;
  wire [3:0] decode_1_pin_3to0, decode_1_pin_bto8;
  wire [11:0] adder_1_out, adder_2_out, and_1_out, divider_1_out, divider_1_rem, divider_2_out,
       divider_2_rem, multiplexer_1_out, multiplexer_2_out, multiplexer_3_out, multiplier_1_out,
       multiplier_2_out, not_1_out, or_1_out, shifter_1_out, shifter_2_out, subtractor_1_out,
       subtractor_2_out, xor_1_out;

  decode decode_1 (
    .Instruction(Instruction), .PIN_Bto8(decode_1_pin_bto8), .PIN_3to0(decode_1_pin_3to0),
    .PIN_1to0(decode_1_pin_1to0));  // open: PIN_7to6, PIN_5to4, PIN_5to0, PIN_3to2
  Adder #(.width(12)) adder_1 (.a(A), .b(B), .out(adder_1_out));  // open: cin, cout
  Subtractor #(.width(12)) subtractor_1 (.a(A), .b(B), .out(subtractor_1_out));  // open: bin, bout
  Multiplier #(.width(12)) multiplier_1 (.a(A), .b(B), .out(multiplier_1_out));  // open: cin, cout
  Divider #(.width(12)) divider_1 (.a(A), .b(B), .out(divider_1_out), .rem(divider_1_rem));  // open: upper
  assign and_1_out = A & B;  // AND_Gate and_1, 12 bits wide
  assign or_1_out = A | B;  // OR_Gate or_1, 12 bits wide
  assign xor_1_out = A ^ B;  // XOR_Gate xor_1, 12 bits wide
  assign not_1_out = ~A;  // NOT_Gate not_1, 12 bits wide
  Adder #(.width(12)) adder_2 (.a(A), .b({{8{1'b0}}, decode_1_pin_3to0}), .out(adder_2_out));  // open: cin, cout
  Subtractor #(.width(12)) subtractor_2 (
    .a(A), .b({{8{1'b0}}, decode_1_pin_3to0}), .out(subtractor_2_out));  // open: bin, bout
  Multiplier #(.width(12)) multiplier_2 (
    .a(A), .b({{8{1'b0}}, decode_1_pin_3to0}), .out(multiplier_2_out));  // open: cin, cout
  Divider #(.width(12)) divider_2 (
    .a(A), .b({{8{1'b0}}, decode_1_pin_3to0}), .out(divider_2_out), .rem(divider_2_rem));  // open: upper
  Shifter #(.width(12)) shifter_1 (.in(A), .\dist (decode_1_pin_3to0), .out(shifter_1_out));
  Shifter #(.shift("lr"), .width(12)) shifter_2 (.in(A), .\dist (decode_1_pin_3to0), .out(shifter_2_out));
  Multiplexer #(.select(2), .width(12)) multiplexer_1 (
    .in0({12{1'b0}}), .in1(adder_1_out), .in2(subtractor_1_out), .in3(multiplier_1_out),
    .out(multiplexer_1_out), .sel(decode_1_pin_1to0));
  Multiplexer #(.select(2), .width(12)) multiplexer_2 (
    .in0(divider_1_out), .in1(divider_1_rem), .in2(and_1_out), .in3(or_1_out), .out(multiplexer_2_out),
    .sel(decode_1_pin_1to0));
  Multiplexer #(.select(2), .width(12)) multiplexer_3 (
    .in0(xor_1_out), .in1({12{1'b0}}), .in2({12{1'b0}}), .in3(not_1_out), .out(multiplexer_3_out),
    .sel(decode_1_pin_1to0));
  Multiplexer #(.select(4), .width(12)) multiplexer_4 (
    .in0(multiplexer_1_out), .in1(multiplexer_2_out), .in2(multiplexer_3_out), .in3(adder_2_out),
    .in4(subtractor_2_out), .in5(multiplier_2_out), .in6(divider_2_out), .in7(divider_2_rem),
    .in8(shifter_1_out), .in9(shifter_2_out), .in10(adder_2_out), .in11(adder_2_out), .in12({12{1'b0}}),
    .in13({12{1'b0}}), .in14({12{1'b0}}), .in15({12{1'b0}}), .out(Result), .sel(decode_1_pin_bto8));
endmodule

module Registers (
  input  Clk,
  input  [1:0] rs1,
  input  [1:0] rs2,
  input  [1:0] rd,
  input  Write_en,
  input  [11:0] Data,
  output [11:0] A,
  output [11:0] B
);

  wire demultiplexer_1_out0, demultiplexer_1_out1, demultiplexer_1_out2, demultiplexer_1_out3;
  wire [11:0] demultiplexer_2_out0, demultiplexer_2_out1, demultiplexer_2_out2, demultiplexer_2_out3, reg0_q,
       reg1_q, reg2_q, reg3_q;

  Demultiplexer #(.select(2)) demultiplexer_1 (
    .out0(demultiplexer_1_out0), .out1(demultiplexer_1_out1), .out2(demultiplexer_1_out2),
    .out3(demultiplexer_1_out3), .in(Write_en), .sel(rd));
  Demultiplexer #(.select(2), .width(12)) demultiplexer_2 (
    .out0(demultiplexer_2_out0), .out1(demultiplexer_2_out1), .out2(demultiplexer_2_out2),
    .out3(demultiplexer_2_out3), .in(Data), .sel(rd));
  Register #(.trigger("falling"), .width(12)) reg0 (
    .D(demultiplexer_2_out0), .en(demultiplexer_1_out0), .clk(Clk), .Q(reg0_q));  // open: clr
  Register #(.trigger("falling"), .width(12)) reg1 (
    .D(demultiplexer_2_out1), .en(demultiplexer_1_out1), .clk(Clk), .Q(reg1_q));  // open: clr
  Register #(.trigger("falling"), .width(12)) reg2 (
    .D(demultiplexer_2_out2), .en(demultiplexer_1_out2), .clk(Clk), .Q(reg2_q));  // open: clr
  Register #(.trigger("falling"), .width(12)) reg3 (
    .D(demultiplexer_2_out3), .en(demultiplexer_1_out3), .clk(Clk), .Q(reg3_q));  // open: clr
  Multiplexer #(.select(2), .width(12)) multiplexer_1 (
    .in0(reg0_q), .in1(reg1_q), .in2(reg2_q), .in3(reg3_q), .out(A), .sel(rs1));
  Multiplexer #(.select(2), .width(12)) multiplexer_2 (
    .in0(reg0_q), .in1(reg1_q), .in2(reg2_q), .in3(reg3_q), .out(B), .sel(rs2));
endmodule

module Branch_unit (
  input  [11:0] IR,
  input  [11:0] NPC_in,
  input  [11:0] A,
  output is_instr_branch,
  output is_taken_branch,
  output [11:0] Result,
  output [11:0] NPC
);

  wire comparator_1_eq, multiplexer_9_out, multiplexer_10_out, multiplexer_11_out, multiplexer_13_out,
       multiplexer_14_out, multiplexer_15_out, not_1_out;
  wire [1:0] decode_1_pin_1to0;
  wire [3:0] decode_1_pin_3to0, decode_1_pin_bto8;
  wire [5:0] decode_1_pin_5to0;
  wire [11:0] adder_1_out, adder_2_out, multiplexer_1_out, multiplexer_2_out, multiplexer_3_out,
       multiplexer_5_out, multiplexer_6_out, multiplexer_7_out, subtractor_1_out;

  decode decode_1 (
    .Instruction(IR), .PIN_Bto8(decode_1_pin_bto8), .PIN_5to0(decode_1_pin_5to0),
    .PIN_3to0(decode_1_pin_3to0), .PIN_1to0(decode_1_pin_1to0));  // open: PIN_7to6, PIN_5to4, PIN_3to2
  Adder #(.width(12)) adder_1 (
    .a({{7{decode_1_pin_5to0[5]}}, decode_1_pin_5to0[4:0]}), .b(NPC_in), .out(adder_1_out));  // open: cin, cout
  Subtractor #(.width(12)) subtractor_1 (.a(adder_1_out), .b(12'h1), .out(subtractor_1_out));  // open: bin, bout
  Adder #(.width(12)) adder_2 (.a({{8{1'b0}}, decode_1_pin_3to0}), .b(A), .out(adder_2_out));  // open: cin, cout
  Multiplexer #(.select(2), .width(12)) multiplexer_1 (
    .in0(NPC_in), .in1(NPC_in), .in2(NPC_in), .in3(NPC_in), .out(multiplexer_1_out), .sel(decode_1_pin_1to0));
  Multiplexer #(.select(2), .width(12)) multiplexer_2 (
    .in0(NPC_in), .in1(NPC_in), .in2(NPC_in), .in3(NPC_in), .out(multiplexer_2_out), .sel(decode_1_pin_1to0));
  Multiplexer #(.select(2), .width(12)) multiplexer_3 (
    .in0(NPC_in), .in1(NPC_in), .in2(NPC_in), .in3(NPC_in), .out(multiplexer_3_out), .sel(decode_1_pin_1to0));
  Multiplexer #(.select(4), .width(12)) multiplexer_4 (
    .in0(multiplexer_1_out), .in1(multiplexer_2_out), .in2(multiplexer_3_out), .in3(NPC_in), .in4(NPC_in),
    .in5(NPC_in), .in6(NPC_in), .in7(NPC_in), .in8(NPC_in), .in9(NPC_in), .in10(NPC_in), .in11(NPC_in),
    .in12(adder_2_out), .in13(subtractor_1_out), .in14(subtractor_1_out), .in15(subtractor_1_out), .out(NPC),
    .sel(decode_1_pin_bto8));
  Comparator #(.width(12)) comparator_1 (.a({12{1'b0}}), .b(A), .eq(comparator_1_eq));  // open: gt, lt
  Multiplexer #(.select(2), .width(12)) multiplexer_5 (
    .in0({12{1'b0}}), .in1({12{1'b0}}), .in2({12{1'b0}}), .in3({12{1'b0}}), .out(multiplexer_5_out),
    .sel(decode_1_pin_1to0));
  Multiplexer #(.select(2), .width(12)) multiplexer_6 (
    .in0({12{1'b0}}), .in1({12{1'b0}}), .in2({12{1'b0}}), .in3({12{1'b0}}), .out(multiplexer_6_out),
    .sel(decode_1_pin_1to0));
  Multiplexer #(.select(2), .width(12)) multiplexer_7 (
    .in0({12{1'b0}}), .in1({12{1'b0}}), .in2({12{1'b0}}), .in3({12{1'b0}}), .out(multiplexer_7_out),
    .sel(decode_1_pin_1to0));
  not not_1 (not_1_out, comparator_1_eq);
  Multiplexer #(.select(4), .width(12)) multiplexer_8 (
    .in0(multiplexer_5_out), .in1(multiplexer_6_out), .in2(multiplexer_7_out), .in3({12{1'b0}}),
    .in4({12{1'b0}}), .in5({12{1'b0}}), .in6({12{1'b0}}), .in7({12{1'b0}}), .in8({12{1'b0}}),
    .in9({12{1'b0}}), .in10({12{1'b0}}), .in11({12{1'b0}}), .in12(NPC_in), .in13(NPC_in), .in14({12{1'b0}}),
    .in15({12{1'b0}}), .out(Result), .sel(decode_1_pin_bto8));
  Multiplexer #(.select(2)) multiplexer_9 (
    .in0(1'b0), .in1(1'b0), .in2(1'b0), .in3(1'b0), .out(multiplexer_9_out), .sel(decode_1_pin_1to0));
  Multiplexer #(.select(2)) multiplexer_10 (
    .in0(1'b0), .in1(1'b0), .in2(1'b0), .in3(1'b0), .out(multiplexer_10_out), .sel(decode_1_pin_1to0));
  Multiplexer #(.select(2)) multiplexer_11 (
    .in0(1'b0), .in1(1'b0), .in2(1'b0), .in3(1'b0), .out(multiplexer_11_out), .sel(decode_1_pin_1to0));
  Multiplexer #(.select(4)) multiplexer_12 (
    .in0(multiplexer_9_out), .in1(multiplexer_10_out), .in2(multiplexer_11_out), .in3(1'b0), .in4(1'b0),
    .in5(1'b0), .in6(1'b0), .in7(1'b0), .in8(1'b0), .in9(1'b0), .in10(1'b0), .in11(1'b0), .in12(1'b1),
    .in13(1'b1), .in14(comparator_1_eq), .in15(not_1_out), .out(is_taken_branch), .sel(decode_1_pin_bto8));
  Multiplexer #(.select(2)) multiplexer_13 (
    .in0(1'b0), .in1(1'b0), .in2(1'b0), .in3(1'b0), .out(multiplexer_13_out), .sel(decode_1_pin_1to0));
  Multiplexer #(.select(2)) multiplexer_14 (
    .in0(1'b0), .in1(1'b0), .in2(1'b0), .in3(1'b0), .out(multiplexer_14_out), .sel(decode_1_pin_1to0));
  Multiplexer #(.select(2)) multiplexer_15 (
    .in0(1'b0), .in1(1'b0), .in2(1'b0), .in3(1'b0), .out(multiplexer_15_out), .sel(decode_1_pin_1to0));
  Multiplexer #(.select(4)) multiplexer_16 (
    .in0(multiplexer_13_out), .in1(multiplexer_14_out), .in2(multiplexer_15_out), .in3(1'b0), .in4(1'b0),
    .in5(1'b0), .in6(1'b0), .in7(1'b0), .in8(1'b0), .in9(1'b0), .in10(1'b0), .in11(1'b0), .in12(1'b1),
    .in13(1'b1), .in14(1'b1), .in15(1'b1), .out(is_instr_branch), .sel(decode_1_pin_bto8));
endmodule

module decode (
  input  [11:0] Instruction,
  output [3:0] PIN_Bto8,
  output [1:0] PIN_7to6,
  output [1:0] PIN_5to4,
  output [5:0] PIN_5to0,
  output [1:0] PIN_3to2,
  output [3:0] PIN_3to0,
  output [1:0] PIN_1to0
);


  assign PIN_1to0 = Instruction[1:0];
  assign PIN_3to0 = Instruction[3:0];
  assign PIN_3to2 = Instruction[3:2];
  assign PIN_5to0 = Instruction[5:0];
  assign PIN_5to4 = Instruction[5:4];
  assign PIN_7to6 = Instruction[7:6];
  assign PIN_Bto8 = Instruction[11:8];
endmodule

module Horloge (
  input  Clk_in,
  input  [11:0] Data,
  input  [11:0] Listen_address,
  input  En,
  output Clk_out,
  output [11:0] Count
);

  wire and_1_out, comparator_1_eq, comparator_2_eq, not_1_out, register_1_q;
  wire [11:0] adder_1_out;

  Comparator #(.width(12)) comparator_1 (.a(Data), .b({12{1'b0}}), .eq(comparator_1_eq));  // open: gt, lt
  Comparator #(.width(12)) comparator_2 (.a(Listen_address), .b({12{1'b1}}), .eq(comparator_2_eq));  // open: gt, lt
  and and_1 (and_1_out, comparator_1_eq, comparator_2_eq, En);
  Register #(.width(1)) register_1 (.D(and_1_out), .en(and_1_out), .clk(Clk_in), .Q(register_1_q));  // open: clr
  not not_1 (not_1_out, register_1_q);
  and and_2 (Clk_out, Clk_in, not_1_out);
  Register #(.width(12)) register_2 (.D(adder_1_out), .en(1'b1), .clk(Clk_out), .Q(Count));  // open: clr
  Adder #(.width(12)) adder_1 (.a(Count), .b(12'h1), .out(adder_1_out));  // open: cin, cout
endmodule

module BCD_7S (
  input  [3:0] Data,
  output A,
  output B,
  output C,
  output D,
  output E,
  output F,
  output G
);

  Multiplexer #(.select(4), .width(7)) multiplexer_1 (
    .in0(7'b0111111), .in1(7'b0000110), .in2(7'b1011011), .in3(7'b1001111), .in4(7'b1100110),
    .in5(7'b1101101), .in6(7'b1111101), .in7(7'b0000111), .in8({7{1'b1}}), .in9(7'b1100111),
    .in10(7'b1110111), .in11(7'b1111100), .in12(7'b0111001), .in13(7'b1011110), .in14(7'b1111001),
    .in15(7'b1110001), .out({G, F, E, D, C, B, A}), .sel(Data));
endmodule

module Periph_listener (
  input  Clk,
  input  [11:0] Data,
  input  [11:0] Address,
  input  En,
  output [3:0] address_000_value_3to0,
  output [3:0] address_000_value_7to4,
  output [3:0] address_000_value_Bto8,
  output [3:0] address_001_value_3to0,
  output [3:0] address_001_value_7to4,
  output [3:0] address_001_value_Bto8,
  output [3:0] address_002_value_3to0,
  output [3:0] address_002_value_7to4,
  output [3:0] address_002_value_Bto8
);

  wire and_1_out, and_2_out, and_3_out, comparator_1_eq, comparator_2_eq, comparator_3_eq;

  Comparator #(.width(12)) comparator_1 (.a(Address), .b({12{1'b0}}), .eq(comparator_1_eq));  // open: gt, lt
  Comparator #(.width(12)) comparator_2 (.a(Address), .b(12'h1), .eq(comparator_2_eq));  // open: gt, lt
  Comparator #(.width(12)) comparator_3 (.a(Address), .b(12'h2), .eq(comparator_3_eq));  // open: gt, lt
  Register #(.width(12)) register_1 (
    .D(Data), .en(and_1_out), .clk(Clk),
    .Q({address_000_value_Bto8, address_000_value_7to4, address_000_value_3to0}));  // open: clr
  and and_1 (and_1_out, comparator_1_eq, En);
  Register #(.width(12)) register_2 (
    .D(Data), .en(and_2_out), .clk(Clk),
    .Q({address_001_value_Bto8, address_001_value_7to4, address_001_value_3to0}));  // open: clr
  and and_2 (and_2_out, comparator_2_eq, En);
  Register #(.width(12)) register_3 (
    .D(Data), .en(and_3_out), .clk(Clk),
    .Q({address_002_value_Bto8, address_002_value_7to4, address_002_value_3to0}));  // open: clr
  and and_3 (and_3_out, comparator_3_eq, En);
endmodule
